// Logisim project decodificador_vga.circ as structural Verilog: 1 circuit, main circuit main
module main (
  input  A15,
  input  S15,
  input  A14,
  input  S14,
  input  A13,
  input  S13,
  output ENABLE
);

  wire or_1_out, xor_1_out, xor_2_out, xor_3_out;

  xor xor_1 (xor_1_out, A15, S15);
  xor xor_2 (xor_2_out, A14, S14);
  xor xor_3 (xor_3_out, A13, S13);
  or or_1 (or_1_out, xor_1_out, xor_2_out);
  or or_2 (ENABLE, or_1_out, xor_3_out);
endmodule
